# Fritzing sketch TVLight (saved by Fritzing 0.9.2b)
breadboards: 1

parts:
  Arduino = Arduino Uno (Rev3)
  R1 = Resistor [tolerance=±5% resistance=220 package=THT]
  LED1 = LED - 5mm [color="Blue (505nm)" package="5 mm [THT]"]

nets:
  N1: Arduino.D9_PWM, LED1.anode
  N2: Arduino.GND, R1.Pin_1
  N3: R1.Pin_0, LED1.cathode
