# Fritzing sketch WelderLight (saved by Fritzing 0.9.2b)
breadboards: 1

parts:
  Arduino = Arduino Uno (Rev3)
  R1 = Resistor [tolerance=±5% resistance=220 package=THT]
  R2 = Resistor [tolerance=±5% resistance=220 package=THT]
  LED1 = LED - 5mm [color="Blue (505nm)" package="5 mm [THT]"]
  SP1 = SPEAKER [package=pcb_mount_speaker]

nets:
  N1: Arduino.D9_PWM, LED1.anode
  N2: Arduino.GND, R1.Pin_1, SP1.+
  N3: Arduino.D6_PWM, R2.Pin_0
  N4: R1.Pin_0, LED1.cathode
  N5: R2.Pin_1, SP1.-
